# Fritzing sketch can_tester (saved by Fritzing 1.0.2b)
breadboards: 1

parts:
  Part1 = Arduino Uno (Rev3)
  M1 = Niren can bus module [package=THT]
  M2 = Niren can bus module [package=THT]

nets:
  N1: Part1.D10_PWM/SS, M1.pin3
  N2: Part1.D11_PWM/MOSI, M2.pin5
  N3: Part1.D12/MISO, M1.pin4, M2.pin4
  N4: Part1.D13/SCK, M1.pin6, M2.pin6
  N5: Part1.D3_PWM, M2.pin7
  N6: Part1.D4, M2.pin3
  N7: Part1.5V, M1.pin1, M2.pin1
  N8: Part1.GND, M1.pin2, M2.pin2
  N9: M1.pin11, M1.pin13, M2.pin12
  N10: M1.pin12, M2.pin13

notes:
  Sender
  Receiver

custom parts:
  Niren can bus module: Niren can bus module availabe on ebay and others. Pcb view assumes that you unsolder the 7 pin header and resolder it on the bottom of the module to connect to the pcb. The two jumpers and the can bus connector remain on the top of the board and don't appear in pcb view.
