# Fritzing sketch tachometer (saved by Fritzing 1.0.2b)
breadboards: 2

parts:
  Part1 = Arduino Pro Mini v13
  M1 = Niren can bus module [package=THT]
  S1 = Square Pushbutton
  M2 = Stepper Motor - Automotive Gauge  # not connected
  M3 = RioRand LM2596

nets:
  N1: Part1.GND, S1.leg0
  N2: Part1.D13/SCK, M1.pin6
  N3: Part1.D12/MISO, M1.pin4
  N4: Part1.D11_PWM/MOSI, M1.pin5
  N5: Part1.D10_PWM/SS, M1.pin3
  N6: Part1.D8, S1.leg1
  N7: Part1.D2, M1.pin7
  N8: M1.pin1, M3.Pin_3
  N9: M1.pin2, M3.Pin_4

custom parts:
  Niren can bus module: Niren can bus module availabe on ebay and others. Pcb view assumes that you unsolder the 7 pin header and resolder it on the bottom of the module to connect to the pcb. The two jumpers and the can bus connector remain on the top of the board and don't appear in pcb view.
  Stepper Motor - Automotive Gauge: Simple, Automotive Gauge stepper motor
