# Fritzing sketch toggle_tester (saved by Fritzing 1.0.2b)
breadboards: 1

parts:
  Part1 = Arduino Uno (Rev3)
  S2 = SPST Switch [package=switch-spdt]

nets:
  N1: Part1.D2, S2.P
  N2: Part1.5V, S2.S
  N3: Part1.GND, S2.O
