# Fritzing sketch x27_168_tester (saved by Fritzing 1.0.2b)
breadboards: 1

parts:
  M1 = Stepper Motor - Automotive Gauge
  Part1 = Arduino Uno (Rev3)
  ENCODER1 = Rotary Encoder with Knob

nets:
  N1: M1.pin_1, Part1.D9_PWM
  N2: M1.pin_2, Part1.D8
  N3: M1.pin_3, Part1.D11_PWM/MOSI
  N4: M1.pin_4, Part1.D10_PWM/SS
  N5: Part1.D2, ENCODER1.no_name_yet#1
  N6: Part1.D3_PWM, ENCODER1.no_name_yet#2
  N7: Part1.D4, ENCODER1.no_name_yet#3
  N8: Part1.5V, ENCODER1.no_name_yet#4
  N9: Part1.GND, ENCODER1.no_name_yet#5

custom parts:
  Stepper Motor - Automotive Gauge: Simple, Automotive Gauge stepper motor
  Rotary Encoder with Knob: Rotary Encoder with 1/4" Shaft and Knob
